# Fritzing sketch Componentes Turtle (saved by Fritzing 0.9.3b)
breadboards: 1

parts:
  Componente2 = Arduino Uno (Rev3)
  Raspberry_Pi_1 = Raspberry Pi 3 [part_number=RPI-3-V1.2]  # not connected
  M1 = DC Motor
  M2 = DC Motor
  U1 = LIPO-1000mAh [package=lipo-1000]
  IC1 = L293D [package=THT]

nets:
  N1: Componente2.D8, IC1.In_4
  N2: Componente2.D9_PWM, IC1.In_2
  N3: Componente2.D10_PWM/SS, IC1.In_1
  N4: Componente2.D5_PWM, IC1.Enable_2
  N5: Componente2.D6_PWM, IC1.Enable_1
  N6: Componente2.D7, IC1.In_3
  N7: Componente2.5V, U1.+, IC1.+Vmotor, IC1.+V
  N8: Componente2.GND, U1.-, IC1.0V
  N9: M1.pin_1, IC1.Out_3_(_Controlled_by_Enable_2_)
  N10: M1.pin_2, IC1.Out_4_(_Controlled_by_Enable_2_)
  N11: M2.pin_1, IC1.Out_2_(_Controlled_by_Enable_1_)
  N12: M2.pin_2, IC1.Out_1_(_Controlled_by_Enable_1_)
